# Fritzing sketch IMU_Setup (saved by Fritzing 0.9.8b)

parts:
  Adafruit#1 = Adafruit LSM6DS3TR-C [part_number=4503]
  Adafruit#2 = Adafruit LSM6DS3TR-C [part_number=4503]  # not connected
  Part1 = Arduino Uno (Rev3)

nets:
  GND: Adafruit#1.GND, Part1.GND
  VCC: Adafruit#1.VCC, Part1.5V
  N1: Adafruit#1.SDA, Part1.A4/SDA
  N2: Adafruit#1.SCL, Part1.A5/SCL

notes:
  IMU 1: I2C Address 0x6A
  IMU 2: I2C Address 0x6B

custom parts:
  Adafruit LSM6DS3TR-C: Add motion and orientation sensing to your Arduino project with this affordable 6 Degree of Freedom (6-DoF) sensor with sensors from ST. The board includes an ST LSM6DS3TR-C, a great entry-level 6-DoF IMU accelerometer + gyro. The 3-axis accelerometer can tell you which direction is down towards the Earth (by measuring gravity) or how fast the board is accelerating in 3D space. The 3-axis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
