# Fritzing sketch Motor Pinout with Breadboard (saved by Fritzing 0.9.8b)
breadboards: 1

parts:
  Part3 = Arduino Uno (Rev3)
  DC_Mot_Enc1 = DC Motor with two-phase hall-encoder [part_number=VT-E-G25A-06-177E]
  Part4 = Motor Driver 1A Dual TB6612FNG  # not connected

nets:
  N1: Part3.D2, DC_Mot_Enc1.pin5
  N2: Part3.D3_PWM, DC_Mot_Enc1.pin2

notes:
  12 V, 3 amp DC power supply; negative lead connects to second Arduino ground
