# Fritzing sketch Motor pinout (saved by Fritzing 0.9.10b)

parts:
  Part2 = Arduino Uno (Rev3)
  DC_Mot_Enc1 = DC Motor with two-phase hall-encoder [part_number=VT-E-G25A-06-177E]
  Part3 = Motor Driver 1A Dual TB6612FNG

nets:
  N1: Part2.D8, Part3.AIN1
  N2: Part2.D9_PWM, Part3.PWMA
  N3: Part2.D2, DC_Mot_Enc1.pin5
  N4: Part2.D3_PWM, DC_Mot_Enc1.pin2
  N5: Part2.D7, Part3.AIN2
  5V: Part2.5V, DC_Mot_Enc1.pin3, Part3.VCC, Part3.STBY
  GND: Part2.GND, DC_Mot_Enc1.pin4, Part3.GND
  N6: DC_Mot_Enc1.pin1, Part3.A01
  N7: DC_Mot_Enc1.pin6, Part3.A02
